// Logisim project mips.circ as structural Verilog: 35 circuits, main circuit sign_extender
module sign_extender (
  input  [15:0] In,
  output [31:0] Out
);

  assign Out = {{16{In[15]}}, In};  // Bit_Extender bit_extender_1
endmodule

module shift_left_by2 (
  input  [31:0] In,
  output [31:0] Out
);

  Shifter #(.width(32)) shifter_1 (.in(In), .\dist (5'b00010), .out(Out));
endmodule

module select_write_regis (
  input  [4:0] A,
  input  [4:0] B,
  input  select,
  output [4:0] O
);

  Multiplexer #(.width(5), .enable("false")) multiplexer_1 (.in0(A), .in1(B), .out(O), .sel(select));
endmodule

module mux2_1 (
  input  A,
  input  B,
  input  Select,
  output O
);

  Multiplexer #(.enable("false")) multiplexer_1 (.in0(A), .in1(B), .out(O), .sel(Select));
endmodule

module control_unit (
  input  [5:0] Opcode,
  output RegDst,
  output Mem_to_reg,
  output Mem_read,
  output Mem_Write,
  output jump,
  output Branch,
  output Sign_zero,
  output [1:0] Alu_op,
  output Alu_Src,
  output Reg_write
);

  wire and_1_out, and_2_out, and_4_out, and_5_out, and_6_out, and_7_out, and_8_out, and_9_out, and_16_out,
       not_1_out, not_2_out, not_3_out, not_4_out, not_5_out, not_6_out, not_8_out, not_9_out, not_10_out,
       not_11_out, not_12_out, not_13_out, not_14_out, not_15_out, not_16_out, not_17_out, not_18_out,
       not_19_out, not_20_out, not_21_out, not_22_out, not_23_out, not_24_out, not_25_out, not_26_out,
       not_27_out, not_28_out, not_29_out, not_30_out, not_31_out, not_32_out, not_34_out, or_1_out,
       or_2_out, or_3_out, or_5_out, or_6_out, or_7_out, or_8_out, or_9_out, or_10_out;

  not not_1 (not_1_out, Opcode[5]);
  not not_2 (not_2_out, Opcode[0]);
  and and_1 (and_1_out, not_1_out, Opcode[3], Opcode[2], Opcode[1], not_2_out);
  not not_3 (not_3_out, Opcode[2]);
  not not_4 (not_4_out, Opcode[3]);
  and and_2 (and_2_out, Opcode[5], not_4_out, not_3_out, Opcode[1], Opcode[0]);
  or or_1 (or_1_out, Opcode[5], Opcode[3], Opcode[2], Opcode[1], Opcode[0]);
  not not_5 (not_5_out, or_1_out);
  not not_6 (not_6_out, Opcode[1]);
  or or_2 (or_2_out, Opcode[5], Opcode[3], Opcode[2], not_6_out, Opcode[0]);
  not not_7 (jump, or_2_out);
  not not_8 (not_8_out, Opcode[4]);
  and and_3 (Reg_write, not_8_out, or_3_out);
  or or_3 (or_3_out, not_5_out, and_2_out, and_1_out);
  not not_9 (not_9_out, Opcode[3]);
  not not_10 (not_10_out, Opcode[5]);
  not not_11 (not_11_out, Opcode[0]);
  not not_12 (not_12_out, Opcode[1]);
  not not_13 (not_13_out, Opcode[3]);
  not not_14 (not_14_out, Opcode[2]);
  and and_4 (and_4_out, Opcode[0], not_14_out, Opcode[5], Opcode[3]);
  not not_15 (not_15_out, Opcode[2]);
  not not_16 (not_16_out, Opcode[0]);
  not not_17 (not_17_out, Opcode[5]);
  not not_18 (not_18_out, Opcode[1]);
  not not_19 (not_19_out, Opcode[3]);
  not not_20 (not_20_out, Opcode[4]);
  and and_5 (and_5_out, not_11_out, Opcode[1], Opcode[3]);
  and and_6 (and_6_out, Opcode[0], not_12_out, not_13_out);
  and and_7 (and_7_out, Opcode[0], not_15_out, Opcode[5], not_9_out);
  and and_8 (and_8_out, not_16_out, Opcode[2], Opcode[3], not_17_out);
  not not_21 (not_21_out, Opcode[4]);
  not not_22 (not_22_out, Opcode[4]);
  not not_23 (not_23_out, Opcode[4]);
  not not_24 (not_24_out, Opcode[5]);
  and and_9 (and_9_out, Opcode[2], not_20_out, not_10_out);
  or or_4 (Alu_op[0], and_9_out, or_5_out);
  or or_5 (or_5_out, and_5_out, and_6_out);
  or or_6 (or_6_out, and_4_out, and_7_out, and_8_out);
  not not_25 (not_25_out, Opcode[2]);
  not not_26 (not_26_out, Opcode[3]);
  not not_27 (not_27_out, Opcode[4]);
  not not_28 (not_28_out, Opcode[2]);
  not not_29 (not_29_out, Opcode[5]);
  not not_30 (not_30_out, Opcode[0]);
  not not_31 (not_31_out, or_7_out);
  or or_7 (or_7_out, Opcode[0], Opcode[4], Opcode[5]);
  not not_32 (not_32_out, Opcode[4]);
  and and_10 (Alu_Src, not_32_out, Opcode[1], or_6_out);
  or or_8 (or_8_out, Opcode[0], Opcode[1], Opcode[2], Opcode[4], Opcode[5], Opcode[3]);
  and and_11 (Mem_Write, Opcode[0], Opcode[1], not_28_out, Opcode[3], not_21_out, Opcode[5]);
  and and_12 (Sign_zero, not_30_out, Opcode[1], Opcode[2], Opcode[3], not_23_out, not_24_out);
  not not_33 (RegDst, or_8_out);
  and and_13 (Mem_read, not_25_out, Opcode[0], Opcode[1], not_26_out, not_27_out, Opcode[5]);
  and and_14 (Branch, Opcode[0], not_18_out, Opcode[2], not_19_out, not_22_out, not_29_out);
  and and_15 (Alu_op[1], not_31_out, or_10_out);
  and and_16 (and_16_out, Opcode[1], Opcode[2], Opcode[3]);
  or or_9 (or_9_out, Opcode[1], Opcode[2], Opcode[3]);
  or or_10 (or_10_out, and_16_out, not_34_out);
  not not_34 (not_34_out, or_9_out);

  assign Mem_to_reg = Mem_read;
endmodule

module alu_control_unit (
  input  [1:0] Alu_op,
  input  [5:0] Func,
  output [1:0] Alu_control
);

  wire and_1_out, and_2_out, and_3_out, and_4_out, and_5_out, not_1_out, not_2_out, not_3_out, not_4_out,
       not_5_out, not_6_out, or_1_out;

  not not_1 (not_1_out, Func[2]);
  not not_2 (not_2_out, Alu_op[0]);
  not not_3 (not_3_out, Func[4]);
  not not_4 (not_4_out, Func[0]);
  and and_1 (and_1_out, Alu_op[0], Alu_op[1]);
  and and_2 (and_2_out, Alu_op[1], Func[3], Func[1], Func[5]);
  or or_1 (or_1_out, Alu_op[0], Func[0], Func[2], Func[4]);
  not not_5 (not_5_out, Alu_op[1]);
  not not_6 (not_6_out, or_1_out);
  and and_3 (and_3_out, Alu_op[0], not_5_out);
  and and_4 (and_4_out, Alu_op[1], not_4_out, Func[1], not_2_out, not_1_out, not_3_out, Func[5]);
  and and_5 (and_5_out, and_2_out, not_6_out);
  or or_2 (Alu_control[1], and_3_out, and_4_out);
  // Probe on Alu_control[1]
  or or_3 (Alu_control[0], and_1_out, and_5_out);
  // Probe on Alu_control[0]
endmodule

module jr_control_unit (
  input  [1:0] Alu_op,
  input  [5:0] Func,
  output Jr_control
);

  wire and_1_out, not_1_out, or_1_out;

  and and_1 (and_1_out, Alu_op[1], Func[3]);
  or or_1 (or_1_out, Alu_op[0], Func[0], Func[1], Func[2], Func[4], Func[5]);
  not not_1 (not_1_out, or_1_out);
  and and_2 (Jr_control, and_1_out, not_1_out);
endmodule

module Fcu_circuit (
  input  in_1,
  input  ALUSrc,
  input  MemtoReg,
  input  RegWrite,
  input  MemRead,
  input  MemWrite,
  input  in_7,
  input  in_8,
  input  [1:0] ALUOp_1_0,
  input  flush,
  output ID_RegDst,
  output ID_ALUSrc,
  output ID_MemtoReg,
  output ID_RegWrite,
  output ID_MemRead,
  output ID_MemWrite,
  output ID_Branch,
  output ID_JRControl,
  output [1:0] ID_ALUOp_1_0
);

  wire not_1_out;

  not not_1 (not_1_out, flush);
  and and_1 (ID_RegDst, in_1, not_1_out);
  and and_2 (ID_ALUSrc, ALUSrc, not_1_out);
  and and_3 (ID_MemtoReg, MemtoReg, not_1_out);
  and and_4 (ID_RegWrite, RegWrite, not_1_out);
  and and_5 (ID_MemRead, MemRead, not_1_out);
  and and_6 (ID_MemWrite, MemWrite, not_1_out);
  and and_7 (ID_Branch, in_7, not_1_out);
  and and_8 (ID_JRControl, in_8, not_1_out);
  and and_9 (ID_ALUOp_1_0[0], ALUOp_1_0[0], not_1_out);
  and and_10 (ID_ALUOp_1_0[1], ALUOp_1_0[1], not_1_out);

  // Notes on the sheet:
  //   RegDst
  //   Branch
  //   JRControl
endmodule

module Compare_address (
  input  [4:0] in_1,
  input  [4:0] in_2,
  output out_3
);

  wire or_1_out, or_2_out, or_3_out, or_4_out, xor_1_out, xor_2_out, xor_3_out, xor_4_out, xor_5_out;

  xor xor_1 (xor_1_out, in_1[3], in_2[3]);
  xor xor_2 (xor_2_out, in_1[4], in_2[4]);
  or or_1 (or_1_out, xor_2_out, xor_1_out);
  xor xor_3 (xor_3_out, in_1[2], in_2[2]);
  or or_2 (or_2_out, or_1_out, xor_3_out);
  xor xor_4 (xor_4_out, in_1[1], in_2[1]);
  or or_3 (or_3_out, or_2_out, xor_4_out);
  xor xor_5 (xor_5_out, in_1[0], in_2[0]);
  or or_4 (or_4_out, or_3_out, xor_5_out);
  not not_1 (out_3, or_4_out);

  // Notes on the sheet:
  //   Addr2[4:0]
endmodule

module Forwading_unit (
  input  [4:0] EX_rt_4_0,
  input  [4:0] Ex_rs_4_0,
  input  [4:0] MEM_WriteRegister_4_0,
  input  [4:0] WB_WriteRegister_4_0,
  input  WB_RegWrite,
  input  MEM_RegWrite,
  output [1:0] ForwardA,
  output [1:0] ForwardB
);

  wire and_1_out, andx_i_out, andy1_i_out, andy_i__0_out, compare_address_1_out_3, compare_address_2_out_3,
       compare_address_3_out_3, compare_address_4_out_3, or_1_out, orMEM_WriteReg_i__0_out,
       orMEM_WriteReg_i__1_out, orMEM_WriteReg_i_out, orWB_WriteReg_i__0_out, orWB_WriteReg_i__1_out,
       orWB_WriteReg_i__2_out, orWB_WriteReg_i_out;

  or orMEM_WriteReg_i (orMEM_WriteReg_i_out, MEM_WriteRegister_4_0[3], MEM_WriteRegister_4_0[4]);
  or orWB_WriteReg_i (orWB_WriteReg_i_out, WB_WriteRegister_4_0[3], WB_WriteRegister_4_0[4]);
  or orWB_WriteReg_i__0 (orWB_WriteReg_i__0_out, WB_WriteRegister_4_0[2], orWB_WriteReg_i_out);
  or orMEM_WriteReg_i__0 (orMEM_WriteReg_i__0_out, MEM_WriteRegister_4_0[2], orMEM_WriteReg_i_out);
  or orWB_WriteReg_i__1 (orWB_WriteReg_i__1_out, WB_WriteRegister_4_0[1], orWB_WriteReg_i__0_out);
  or orMEM_WriteReg_i__1 (orMEM_WriteReg_i__1_out, MEM_WriteRegister_4_0[1], orMEM_WriteReg_i__0_out);
  or orWB_WriteReg_i__2 (orWB_WriteReg_i__2_out, WB_WriteRegister_4_0[0], orWB_WriteReg_i__1_out);
  Compare_address compare_address_1 (.in_1(WB_WriteRegister_4_0), .in_2(EX_rt_4_0), .out_3(compare_address_1_out_3));
  Compare_address compare_address_2 (.in_1(WB_WriteRegister_4_0), .in_2(Ex_rs_4_0), .out_3(compare_address_2_out_3));
  or or_1 (or_1_out, orMEM_WriteReg_i__1_out, MEM_WriteRegister_4_0[0]);
  and and_1 (and_1_out, orWB_WriteReg_i__2_out, WB_RegWrite);
  and andy1_i (andy1_i_out, and_1_out, compare_address_1_out_3);
  and andy_i__0 (andy_i__0_out, and_1_out, compare_address_2_out_3);
  Compare_address compare_address_3 (.in_1(MEM_WriteRegister_4_0), .in_2(Ex_rs_4_0), .out_3(compare_address_3_out_3));
  Compare_address compare_address_4 (.in_1(MEM_WriteRegister_4_0), .in_2(EX_rt_4_0), .out_3(compare_address_4_out_3));
  and andx_i (andx_i_out, or_1_out, MEM_RegWrite);
  and NOTxANDy_i (ForwardA[0], ForwardA[1], andy_i__0_out);
  and NOTx1ANDy1_i (ForwardB[0], ForwardB[1], andy1_i_out);
  and andx1_i (ForwardB[1], andx_i_out, compare_address_4_out_3);
  and andx_i__0 (ForwardA[1], andx_i_out, compare_address_3_out_3);
endmodule

module mux3_32_32 (
  input  [31:0] A__31_0,
  input  [31:0] B__31_0,
  input  [31:0] C__31_0,
  input  [1:0] Select__1_0,
  output [31:0] out_5
);

  wire [31:0] multiplexer_1_out, multiplexer_2_out;

  Multiplexer #(.width(32), .enable("false")) multiplexer_1 (
    .in0(A__31_0), .in1(B__31_0), .out(multiplexer_1_out), .sel(Select__1_0[1]));
  Multiplexer #(.width(32), .enable("false")) multiplexer_2 (
    .in0(C__31_0), .in1(A__31_0), .out(multiplexer_2_out), .sel(Select__1_0[1]));
  Multiplexer #(.width(32), .enable("false")) multiplexer_3 (
    .in0(multiplexer_1_out), .in1(multiplexer_2_out), .out(out_5), .sel(Select__1_0[0]));
endmodule

module scu (
  input  [5:0] in_1,
  input  EX_MemRead,
  input  [4:0] in_3,
  input  [4:0] in_4,
  input  [4:0] in_5,
  output Stall_flush,
  output IFID_WriteEn,
  output PC_WriteEn
);

  wire and_1_out, and_2_out, or_1_out, or_2_out, or_3_out, or_4_out, or_5_out, or_6_out, or_7_out, or_8_out,
       or_9_out, or_10_out, or_11_out, or_12_out, or_13_out, or_14_out, or_15_out, or_16_out, or_17_out,
       or_18_out, or_19_out, xor_1_out, xor_2_out, xor_3_out, xor_4_out, xor_5_out, xor_6_out, xor_7_out,
       xor_8_out, xor_9_out, xor_10_out, xor_11_out, xor_12_out, xor_13_out, xor_14_out, xor_15_out;

  xor xor_1 (xor_1_out, in_1[5], 1'b0);
  or or_1 (or_1_out, xor_1_out, in_1[4]);
  or or_2 (or_2_out, in_1[5], in_1[4]);
  xor xor_2 (xor_2_out, in_1[3], 1'b0);
  xor xor_3 (xor_3_out, in_1[2], 1'b0);
  or or_3 (or_3_out, or_1_out, in_1[3]);
  or or_4 (or_4_out, or_2_out, xor_2_out);
  xor xor_4 (xor_4_out, in_4[3], in_5[3]);
  xor xor_5 (xor_5_out, in_4[4], in_5[4]);
  or or_5 (or_5_out, or_3_out, in_1[2]);
  or or_6 (or_6_out, or_4_out, xor_3_out);
  xor xor_6 (xor_6_out, in_1[1], 1'b0);
  xor xor_7 (xor_7_out, in_4[3], in_3[3]);
  xor xor_8 (xor_8_out, in_4[4], in_3[4]);
  xor xor_9 (xor_9_out, in_4[2], in_5[2]);
  or or_7 (or_7_out, xor_5_out, xor_4_out);
  or or_8 (or_8_out, or_5_out, xor_6_out);
  or or_9 (or_9_out, or_6_out, xor_6_out);
  xor xor_10 (xor_10_out, in_1[0], 1'b0);
  or or_10 (or_10_out, xor_8_out, xor_7_out);
  xor xor_11 (xor_11_out, in_4[2], in_3[2]);
  or or_11 (or_11_out, xor_9_out, or_7_out);
  xor xor_12 (xor_12_out, in_4[1], in_5[1]);
  or or_12 (or_12_out, or_8_out, xor_10_out);
  or or_13 (or_13_out, or_9_out, in_1[0]);
  or or_14 (or_14_out, or_10_out, xor_11_out);
  xor xor_13 (xor_13_out, in_4[1], in_3[1]);
  or or_15 (or_15_out, or_11_out, xor_12_out);
  xor xor_14 (xor_14_out, in_4[0], in_5[0]);
  and and_1 (and_1_out, or_12_out, or_13_out);
  or or_16 (or_16_out, or_14_out, xor_13_out);
  xor xor_15 (xor_15_out, in_4[0], in_3[0]);
  or or_17 (or_17_out, or_15_out, xor_14_out);
  or or_18 (or_18_out, or_16_out, xor_15_out);
  and and_2 (and_2_out, and_1_out, or_17_out);
  or or_19 (or_19_out, or_18_out, and_2_out);
  and and_3 (Stall_flush, EX_MemRead, or_19_out);
  not not_1 (IFID_WriteEn, Stall_flush);

  assign PC_WriteEn = IFID_WriteEn;

  // Notes on the sheet:
  //   ID_Op[5:0]
  //   ID_rt[4:0]
  //   ID_rs[4:0]
  //   EX_rt[4:0]
endmodule

module Wb (
  input  [31:0] ReadData1_31_0,
  input  [4:0] rs_4_0,
  input  RegWrite,
  input  [4:0] WriteRegister_4_0,
  input  [31:0] ReadData2_31_0,
  input  [4:0] rt_4_0,
  input  [31:0] WriteData1_31_0,
  output [31:0] ReadData1Out_31_0,
  output [31:0] ReadData2Out_31_0
);

  wire and_1_out, and_2_out, and_3_out, compare_address_1_out_3, compare_address_2_out_3, or_1_out, or_2_out,
       or_3_out, or_4_out;

  or or_1 (or_1_out, WriteRegister_4_0[3], WriteRegister_4_0[4]);
  or or_2 (or_2_out, WriteRegister_4_0[2], or_1_out);
  or or_3 (or_3_out, WriteRegister_4_0[1], or_2_out);
  or or_4 (or_4_out, WriteRegister_4_0[0], or_3_out);
  Compare_address compare_address_1 (.in_1(WriteRegister_4_0), .in_2(rs_4_0), .out_3(compare_address_1_out_3));
  and and_1 (and_1_out, RegWrite, or_4_out);
  Compare_address compare_address_2 (.in_1(WriteRegister_4_0), .in_2(rt_4_0), .out_3(compare_address_2_out_3));
  and and_2 (and_2_out, and_1_out, compare_address_1_out_3);
  and and_3 (and_3_out, and_1_out, compare_address_2_out_3);
  Multiplexer #(.width(32), .enable("false")) multiplexer_1 (
    .in0(ReadData1_31_0), .in1(WriteData1_31_0), .out(ReadData1Out_31_0), .sel(and_2_out));
  Multiplexer #(.width(32), .enable("false")) multiplexer_2 (
    .in0(ReadData2_31_0), .in1(WriteData1_31_0), .out(ReadData2Out_31_0), .sel(and_3_out));
endmodule

module data_memory (
  input  [31:0] addr,
  input  write_enable,
  input  [31:0] write_data,
  output [31:0] data
);

  wire clock_1_out;

  Clock clock_1 (.out(clock_1_out));
  RAM #(.addrWidth(24), .dataWidth(32), .bus("separate")) ram_1 (
    .addr(addr[23:0]), .din(write_data), .data(data), .str(write_enable), .clk(clock_1_out));  // open: sel, ld, clr
endmodule

module mux1 (
  input  A,
  input  B,
  input  sel,
  output O
);

  wire and_1_out, and_2_out, not_1_out;

  not not_1 (not_1_out, sel);
  and and_1 (and_1_out, A, not_1_out);
  and and_2 (and_2_out, B, sel);
  or or_1 (O, and_1_out, and_2_out);
endmodule

module add2 (
  input  A,
  input  B,
  input  cin,
  input  select,
  output out,
  output cout
);

  wire mux1_1_o, not_1_out;

  not not_1 (not_1_out, B);
  mux1 mux1_1 (.A(B), .B(not_1_out), .sel(select), .O(mux1_1_o));
  Adder #(.width(1)) adder_1 (.a(A), .b(mux1_1_o), .out(out), .cin(cin), .cout(cout));
endmodule

module alu1bit (
  input  [1:0] Alucontrol,
  input  a,
  input  b,
  input  carryin,
  input  less,
  output carryout,
  output result
);

  wire add2_1_out, mux1_1_o, xor_1_out;

  xor xor_1 (xor_1_out, a, b);
  add2 add2_1 (.A(a), .B(b), .cin(carryin), .select(Alucontrol[1]), .out(add2_1_out), .cout(carryout));
  mux1 mux1_1 (.A(xor_1_out), .B(less), .sel(Alucontrol[1]), .O(mux1_1_o));
  mux1 mux1_2 (.A(add2_1_out), .B(mux1_1_o), .sel(Alucontrol[0]), .O(result));
endmodule

module alu (
  input  [31:0] BUSSA,
  input  [31:0] BUSSB,
  input  [1:0] ALUControl,
  output [31:0] Output,
  output negative,
  output overflow,
  output carryout,
  output Zero
);

  wire add2_1_out, alu1bit_1_carryout, alu1bit_2_carryout, alu1bit_3_carryout, alu1bit_4_carryout,
       alu1bit_5_carryout, alu1bit_6_carryout, alu1bit_7_carryout, alu1bit_8_carryout, alu1bit_9_carryout,
       alu1bit_10_carryout, alu1bit_11_carryout, alu1bit_12_carryout, alu1bit_13_carryout,
       alu1bit_14_carryout, alu1bit_15_carryout, alu1bit_16_carryout, alu1bit_17_carryout,
       alu1bit_18_carryout, alu1bit_19_carryout, alu1bit_20_carryout, alu1bit_21_carryout,
       alu1bit_22_carryout, alu1bit_23_carryout, alu1bit_24_carryout, alu1bit_25_carryout,
       alu1bit_26_carryout, alu1bit_27_carryout, alu1bit_28_carryout, alu1bit_29_carryout,
       alu1bit_30_carryout, alu1bit_31_carryout, alu1bit_32_carryout, not_1_out, or_1_out, or_2_out,
       or_3_out, or_4_out, or_5_out, or_6_out, or_7_out, or_8_out, or_9_out, or_10_out, or_11_out, or_12_out,
       or_13_out, or_14_out, or_15_out, or_16_out, or_17_out, or_18_out, or_19_out, or_20_out, or_21_out,
       or_22_out, or_23_out, or_24_out, or_25_out, or_26_out, or_27_out, or_28_out, or_29_out, or_30_out,
       or_31_out, xor_1_out;

  add2 add2_1 (
    .A(BUSSA[31]), .B(BUSSB[31]), .cin(alu1bit_32_carryout), .select(ALUControl[1]), .out(add2_1_out));  // open: cout
  alu1bit alu1bit_1 (
    .Alucontrol(ALUControl), .a(BUSSA[1]), .b(BUSSB[1]), .carryin(alu1bit_17_carryout), .less(1'b0),
    .carryout(alu1bit_1_carryout), .result(Output[1]));
  alu1bit alu1bit_2 (
    .Alucontrol(ALUControl), .a(BUSSA[3]), .b(BUSSB[3]), .carryin(alu1bit_18_carryout), .less(1'b0),
    .carryout(alu1bit_2_carryout), .result(Output[3]));
  alu1bit alu1bit_3 (
    .Alucontrol(ALUControl), .a(BUSSA[5]), .b(BUSSB[5]), .carryin(alu1bit_19_carryout), .less(1'b0),
    .carryout(alu1bit_3_carryout), .result(Output[5]));
  alu1bit alu1bit_4 (
    .Alucontrol(ALUControl), .a(BUSSA[7]), .b(BUSSB[7]), .carryin(alu1bit_20_carryout), .less(1'b0),
    .carryout(alu1bit_4_carryout), .result(Output[7]));
  alu1bit alu1bit_5 (
    .Alucontrol(ALUControl), .a(BUSSA[9]), .b(BUSSB[9]), .carryin(alu1bit_21_carryout), .less(1'b0),
    .carryout(alu1bit_5_carryout), .result(Output[9]));
  alu1bit alu1bit_6 (
    .Alucontrol(ALUControl), .a(BUSSA[11]), .b(BUSSB[11]), .carryin(alu1bit_22_carryout), .less(1'b0),
    .carryout(alu1bit_6_carryout), .result(Output[11]));
  alu1bit alu1bit_7 (
    .Alucontrol(ALUControl), .a(BUSSA[13]), .b(BUSSB[13]), .carryin(alu1bit_23_carryout), .less(1'b0),
    .carryout(alu1bit_7_carryout), .result(Output[13]));
  alu1bit alu1bit_8 (
    .Alucontrol(ALUControl), .a(BUSSA[15]), .b(BUSSB[15]), .carryin(alu1bit_24_carryout), .less(1'b0),
    .carryout(alu1bit_8_carryout), .result(Output[15]));
  alu1bit alu1bit_9 (
    .Alucontrol(ALUControl), .a(BUSSA[17]), .b(BUSSB[17]), .carryin(alu1bit_25_carryout), .less(1'b0),
    .carryout(alu1bit_9_carryout), .result(Output[17]));
  alu1bit alu1bit_10 (
    .Alucontrol(ALUControl), .a(BUSSA[19]), .b(BUSSB[19]), .carryin(alu1bit_26_carryout), .less(1'b0),
    .carryout(alu1bit_10_carryout), .result(Output[19]));
  alu1bit alu1bit_11 (
    .Alucontrol(ALUControl), .a(BUSSA[21]), .b(BUSSB[21]), .carryin(alu1bit_27_carryout), .less(1'b0),
    .carryout(alu1bit_11_carryout), .result(Output[21]));
  alu1bit alu1bit_12 (
    .Alucontrol(ALUControl), .a(BUSSA[23]), .b(BUSSB[23]), .carryin(alu1bit_28_carryout), .less(1'b0),
    .carryout(alu1bit_12_carryout), .result(Output[23]));
  alu1bit alu1bit_13 (
    .Alucontrol(ALUControl), .a(BUSSA[25]), .b(BUSSB[25]), .carryin(alu1bit_29_carryout), .less(1'b0),
    .carryout(alu1bit_13_carryout), .result(Output[25]));
  alu1bit alu1bit_14 (
    .Alucontrol(ALUControl), .a(BUSSA[27]), .b(BUSSB[27]), .carryin(alu1bit_30_carryout), .less(1'b0),
    .carryout(alu1bit_14_carryout), .result(Output[27]));
  alu1bit alu1bit_15 (
    .Alucontrol(ALUControl), .a(BUSSA[29]), .b(BUSSB[29]), .carryin(alu1bit_31_carryout), .less(1'b0),
    .carryout(alu1bit_15_carryout), .result(Output[29]));
  alu1bit alu1bit_16 (
    .Alucontrol(ALUControl), .a(BUSSA[31]), .b(BUSSB[31]), .carryin(alu1bit_32_carryout), .less(1'b0),
    .carryout(alu1bit_16_carryout), .result(negative));
  xor xor_1 (xor_1_out, overflow, add2_1_out);
  not not_1 (not_1_out, alu1bit_16_carryout);
  alu1bit alu1bit_17 (
    .Alucontrol(ALUControl), .a(BUSSA[0]), .b(BUSSB[0]), .carryin(ALUControl[1]), .less(xor_1_out),
    .carryout(alu1bit_17_carryout), .result(Output[0]));
  alu1bit alu1bit_18 (
    .Alucontrol(ALUControl), .a(BUSSA[2]), .b(BUSSB[2]), .carryin(alu1bit_1_carryout), .less(1'b0),
    .carryout(alu1bit_18_carryout), .result(Output[2]));
  alu1bit alu1bit_19 (
    .Alucontrol(ALUControl), .a(BUSSA[4]), .b(BUSSB[4]), .carryin(alu1bit_2_carryout), .less(1'b0),
    .carryout(alu1bit_19_carryout), .result(Output[4]));
  alu1bit alu1bit_20 (
    .Alucontrol(ALUControl), .a(BUSSA[6]), .b(BUSSB[6]), .carryin(alu1bit_3_carryout), .less(1'b0),
    .carryout(alu1bit_20_carryout), .result(Output[6]));
  alu1bit alu1bit_21 (
    .Alucontrol(ALUControl), .a(BUSSA[8]), .b(BUSSB[8]), .carryin(alu1bit_4_carryout), .less(1'b0),
    .carryout(alu1bit_21_carryout), .result(Output[8]));
  alu1bit alu1bit_22 (
    .Alucontrol(ALUControl), .a(BUSSA[10]), .b(BUSSB[10]), .carryin(alu1bit_5_carryout), .less(1'b0),
    .carryout(alu1bit_22_carryout), .result(Output[10]));
  alu1bit alu1bit_23 (
    .Alucontrol(ALUControl), .a(BUSSA[12]), .b(BUSSB[12]), .carryin(alu1bit_6_carryout), .less(1'b0),
    .carryout(alu1bit_23_carryout), .result(Output[12]));
  alu1bit alu1bit_24 (
    .Alucontrol(ALUControl), .a(BUSSA[14]), .b(BUSSB[14]), .carryin(alu1bit_7_carryout), .less(1'b0),
    .carryout(alu1bit_24_carryout), .result(Output[14]));
  alu1bit alu1bit_25 (
    .Alucontrol(ALUControl), .a(BUSSA[16]), .b(BUSSB[16]), .carryin(alu1bit_8_carryout), .less(1'b0),
    .carryout(alu1bit_25_carryout), .result(Output[16]));
  alu1bit alu1bit_26 (
    .Alucontrol(ALUControl), .a(BUSSA[18]), .b(BUSSB[18]), .carryin(alu1bit_9_carryout), .less(1'b0),
    .carryout(alu1bit_26_carryout), .result(Output[18]));
  alu1bit alu1bit_27 (
    .Alucontrol(ALUControl), .a(BUSSA[20]), .b(BUSSB[20]), .carryin(alu1bit_10_carryout), .less(1'b0),
    .carryout(alu1bit_27_carryout), .result(Output[20]));
  alu1bit alu1bit_28 (
    .Alucontrol(ALUControl), .a(BUSSA[22]), .b(BUSSB[22]), .carryin(alu1bit_11_carryout), .less(1'b0),
    .carryout(alu1bit_28_carryout), .result(Output[22]));
  alu1bit alu1bit_29 (
    .Alucontrol(ALUControl), .a(BUSSA[24]), .b(BUSSB[24]), .carryin(alu1bit_12_carryout), .less(1'b0),
    .carryout(alu1bit_29_carryout), .result(Output[24]));
  alu1bit alu1bit_30 (
    .Alucontrol(ALUControl), .a(BUSSA[26]), .b(BUSSB[26]), .carryin(alu1bit_13_carryout), .less(1'b0),
    .carryout(alu1bit_30_carryout), .result(Output[26]));
  alu1bit alu1bit_31 (
    .Alucontrol(ALUControl), .a(BUSSA[28]), .b(BUSSB[28]), .carryin(alu1bit_14_carryout), .less(1'b0),
    .carryout(alu1bit_31_carryout), .result(Output[28]));
  alu1bit alu1bit_32 (
    .Alucontrol(ALUControl), .a(BUSSA[30]), .b(BUSSB[30]), .carryin(alu1bit_15_carryout), .less(1'b0),
    .carryout(alu1bit_32_carryout), .result(Output[30]));
  xor xor_2 (overflow, alu1bit_32_carryout, alu1bit_16_carryout);
  mux1 mux1_1 (.A(alu1bit_16_carryout), .B(not_1_out), .sel(ALUControl[1]), .O(carryout));
  or or_1 (or_1_out, Output[0], Output[1]);
  or or_2 (or_2_out, Output[4], Output[5]);
  or or_3 (or_3_out, Output[16], Output[17]);
  or or_4 (or_4_out, Output[20], Output[21]);
  or or_5 (or_5_out, or_1_out, Output[2]);
  or or_6 (or_6_out, or_2_out, Output[6]);
  or or_7 (or_7_out, or_3_out, Output[18]);
  or or_8 (or_8_out, or_4_out, Output[22]);
  or or_9 (or_9_out, Output[8], Output[9]);
  or or_10 (or_10_out, Output[24], Output[25]);
  or or_11 (or_11_out, or_5_out, Output[3]);
  or or_12 (or_12_out, or_6_out, Output[7]);
  or or_13 (or_13_out, or_7_out, Output[19]);
  or or_14 (or_14_out, or_8_out, Output[23]);
  or or_15 (or_15_out, or_9_out, Output[10]);
  or or_16 (or_16_out, or_10_out, Output[26]);
  or or_17 (or_17_out, Output[12], Output[13]);
  or or_18 (or_18_out, Output[28], Output[29]);
  or or_19 (or_19_out, or_11_out, or_12_out);
  or or_20 (or_20_out, or_13_out, or_14_out);
  or or_21 (or_21_out, or_15_out, Output[11]);
  or or_22 (or_22_out, or_16_out, Output[27]);
  or or_23 (or_23_out, or_17_out, Output[14]);
  or or_24 (or_24_out, or_18_out, Output[30]);
  or or_25 (or_25_out, or_19_out, or_21_out);
  or or_26 (or_26_out, or_20_out, or_22_out);
  or or_27 (or_27_out, or_23_out, Output[15]);
  or or_28 (or_28_out, or_24_out, negative);
  or or_29 (or_29_out, or_25_out, or_27_out);
  or or_30 (or_30_out, or_26_out, or_28_out);
  or or_31 (or_31_out, or_29_out, or_30_out);
  not not_2 (Zero, or_31_out);

  assign Output[31] = negative;

  // Other names for the same wires on the sheet: A0 = Output[0]; A1 = Output[1]; A2 = Output[2]; A3 = Output[3];
  //   A4 = Output[4]; A5 = Output[5]; A6 = Output[6]; A7 = Output[7]; A8 = Output[8]; A9 = Output[9];
  //   A10 = Output[10]; A11 = Output[11]; A12 = Output[12]; A13 = Output[13]; A14 = Output[14]; A15 = Output[15];
  //   A16 = Output[16]; A17 = Output[17]; A18 = Output[18]; A19 = Output[19]; A20 = Output[20]; A21 = Output[21];
  //   A22 = Output[22]; A23 = Output[23]; A24 = Output[24]; A25 = Output[25]; A26 = Output[26]; A27 = Output[27];
  //   A28 = Output[28]; A29 = Output[29]; A30 = Output[30]; A31 = negative

  // Notes on the sheet:
  //   BUSA   
  //   BUSA   
endmodule

module zero_extension (
  input  [15:0] in_1,
  output [31:0] out_2
);

  assign out_2 = {{16{1'b0}}, in_1};  // Bit_Extender bit_extender_1
endmodule

module mux2_32_32 (
  input  [31:0] Data0,
  input  [31:0] Data1,
  input  select,
  output [31:0] Dataout
);

  Multiplexer #(.width(32), .enable("false")) multiplexer_1 (.in0(Data0), .in1(Data1), .out(Dataout), .sel(select));
endmodule

module adder_1_bit (
  input  cin,
  input  \input ,
  input  input0,
  output sum,
  output cout
);

  wire and_1_out, and_2_out, xor_1_out;

  and and_1 (and_1_out, \input , input0);
  xor xor_1 (xor_1_out, \input , input0);
  xor xor_2 (sum, xor_1_out, cin);
  and and_2 (and_2_out, xor_1_out, cin);
  or or_1 (cout, and_2_out, and_1_out);
endmodule

module _8bit_adder (
  input  in_1,
  input  [7:0] input8,
  input  [7:0] input81,
  output [7:0] output8,
  output cout8
);

  wire adder_1_bit_1_cout, adder_1_bit_2_cout, adder_1_bit_3_cout, adder_1_bit_4_cout, adder_1_bit_5_cout,
       adder_1_bit_6_cout, adder_1_bit_7_cout;

  adder_1_bit adder_1_bit_1 (
    .\input (input8[0]), .input0(input81[0]), .cin(in_1), .cout(adder_1_bit_1_cout), .sum(output8[0]));
  adder_1_bit adder_1_bit_2 (
    .\input (input8[1]), .input0(input81[1]), .cin(adder_1_bit_1_cout), .cout(adder_1_bit_2_cout),
    .sum(output8[1]));
  adder_1_bit adder_1_bit_3 (
    .\input (input8[2]), .input0(input81[2]), .cin(adder_1_bit_2_cout), .cout(adder_1_bit_3_cout),
    .sum(output8[2]));
  adder_1_bit adder_1_bit_4 (
    .\input (input8[3]), .input0(input81[3]), .cin(adder_1_bit_3_cout), .cout(adder_1_bit_4_cout),
    .sum(output8[3]));
  adder_1_bit adder_1_bit_5 (
    .\input (input8[4]), .input0(input81[4]), .cin(adder_1_bit_4_cout), .cout(adder_1_bit_5_cout),
    .sum(output8[4]));
  adder_1_bit adder_1_bit_6 (
    .\input (input8[5]), .input0(input81[5]), .cin(adder_1_bit_5_cout), .cout(adder_1_bit_6_cout),
    .sum(output8[5]));
  adder_1_bit adder_1_bit_7 (
    .\input (input8[6]), .input0(input81[6]), .cin(adder_1_bit_6_cout), .cout(adder_1_bit_7_cout),
    .sum(output8[6]));
  adder_1_bit adder_1_bit_8 (
    .\input (input8[7]), .input0(input81[7]), .cin(adder_1_bit_7_cout), .cout(cout8), .sum(output8[7]));
endmodule

module _32bit_adder (
  input  Cin,
  input  [31:0] in_2,
  input  [31:0] in_3,
  output [31:0] out_4,
  output Cout
);

  wire n8bit_adder_1_cout8, n8bit_adder_2_cout8, n8bit_adder_3_cout8;

  _8bit_adder u_8bit_adder_1 (
    .input8(in_2[7:0]), .input81(in_3[7:0]), .in_1(Cin), .cout8(n8bit_adder_1_cout8), .output8(out_4[7:0]));
  _8bit_adder u_8bit_adder_2 (
    .input8(in_2[15:8]), .input81(in_3[15:8]), .in_1(n8bit_adder_1_cout8), .cout8(n8bit_adder_2_cout8),
    .output8(out_4[15:8]));
  _8bit_adder u_8bit_adder_3 (
    .input8(in_2[23:16]), .input81(in_3[23:16]), .in_1(n8bit_adder_2_cout8), .cout8(n8bit_adder_3_cout8),
    .output8(out_4[23:16]));
  _8bit_adder u_8bit_adder_4 (
    .input8(in_2[31:24]), .input81(in_3[31:24]), .in_1(n8bit_adder_3_cout8), .cout8(Cout),
    .output8(out_4[31:24]));
endmodule

module d_ff (
  input  d,
  input  reset,
  output q
);

  wire clock_out;

  Clock clock (.out(clock_out));
  D_Flip_Flop d_ff_1 (.clk(clock_out), .D(d), .Q(q), .reset(reset));  // open: Qn, preset, en
endmodule

module reg_1bit (
  input  write_enable,
  input  bit_data,
  input  reset,
  output bitout
);

  wire and_1_out, and_2_out, clock_out, not_1_out, or_1_out;

  Clock clock (.out(clock_out));
  not not_1 (not_1_out, write_enable);
  D_Flip_Flop d_ff_1 (.clk(clock_out), .D(or_1_out), .Q(bitout), .reset(reset));  // open: Qn, preset, en
  and and_1 (and_1_out, write_enable, bit_data);
  // Probe on and_1_out
  // Probe on and_2_out
  and and_2 (and_2_out, not_1_out, bitout);
  or or_1 (or_1_out, and_1_out, and_2_out);
  // Probe on or_1_out
endmodule

module register (
  input  [31:0] reg_in,
  input  enable,
  input  reset,
  output [31:0] \output 
);

  wire clock_out;

  Clock clock (.out(clock_out));
  Register #(.width(32)) register_1 (.D(reg_in), .en(enable), .Q(\output ), .clk(clock_out), .clr(reset));
endmodule

module decoder (
  input  Reg_write,
  input  [4:0] Write_reg,
  output [31:0] write_en
);

  wire [31:0] bit_extender_1_out, dec5to32_1_out_2;

  assign bit_extender_1_out = {{31{Reg_write}}, Reg_write};  // Bit_Extender bit_extender_1
  // Probe on bit_extender_1_out
  dec5to32 dec5to32_1 (.in_1(Write_reg), .out_2(dec5to32_1_out_2));
  // Probe on dec5to32_1_out_2
  assign write_en = bit_extender_1_out & dec5to32_1_out_2;  // AND_Gate and_1, 32 bits wide
endmodule

module and_more (
  input  in_1,
  input  in_2,
  input  in_3,
  input  in_4,
  input  in_5,
  output out_6
);

  and and_1 (out_6, in_1, in_2, in_3, in_4, in_5);
endmodule

module dec5to32 (
  input  [4:0] in_1,
  output [31:0] out_2
);

  Decoder #(.select(5), .enable("false")) decoder_1 (
    .out0(out_2[0]), .out1(out_2[1]), .out2(out_2[2]), .out3(out_2[3]), .out4(out_2[4]), .out5(out_2[5]),
    .out6(out_2[6]), .out7(out_2[7]), .out8(out_2[8]), .out9(out_2[9]), .out10(out_2[10]), .out11(out_2[11]),
    .out12(out_2[12]), .out13(out_2[13]), .out14(out_2[14]), .out15(out_2[15]), .out16(out_2[16]),
    .out17(out_2[17]), .out18(out_2[18]), .out19(out_2[19]), .out20(out_2[20]), .out21(out_2[21]),
    .out22(out_2[22]), .out23(out_2[23]), .out24(out_2[24]), .out25(out_2[25]), .out26(out_2[26]),
    .out27(out_2[27]), .out28(out_2[28]), .out29(out_2[29]), .out30(out_2[30]), .out31(out_2[31]), .sel(in_1));
endmodule

module mux32_1 (
  input  [31:0] in,
  input  [4:0] select,
  output out
);

  Multiplexer #(.select(5), .enable("false")) multiplexer_1 (
    .in0(in[0]), .in1(in[1]), .in2(in[2]), .in3(in[3]), .in4(in[4]), .in5(in[5]), .in6(in[6]), .in7(in[7]),
    .in8(in[8]), .in9(in[9]), .in10(in[10]), .in11(in[11]), .in12(in[12]), .in13(in[13]), .in14(in[14]),
    .in15(in[15]), .in16(in[16]), .in17(in[17]), .in18(in[18]), .in19(in[19]), .in20(in[20]), .in21(in[21]),
    .in22(in[22]), .in23(in[23]), .in24(in[24]), .in25(in[25]), .in26(in[26]), .in27(in[27]), .in28(in[28]),
    .in29(in[29]), .in30(in[30]), .in31(in[31]), .out(out), .sel(select));
endmodule

module mux32_32to32 (
  input  [31:0] in_1,
  input  [31:0] in_2,
  input  [31:0] in_3,
  input  [31:0] in_4,
  input  [31:0] in_5,
  input  [31:0] in_6,
  input  [31:0] in_7,
  input  [31:0] in_8,
  input  [31:0] in_9,
  input  [31:0] in_10,
  input  [31:0] in_11,
  input  [31:0] in_12,
  input  [31:0] in_13,
  input  [31:0] in_14,
  input  [31:0] in_15,
  input  [31:0] in_16,
  input  [31:0] in_17,
  input  [31:0] in_18,
  input  [4:0] in_19,
  input  [31:0] in_20,
  input  [31:0] in_21,
  input  [31:0] in_22,
  input  [31:0] in_23,
  input  [31:0] in_24,
  input  [31:0] in_25,
  input  [31:0] in_26,
  input  [31:0] in_27,
  input  [31:0] in_28,
  input  [31:0] in_29,
  input  [31:0] in_30,
  input  [31:0] in_31,
  input  [31:0] in_32,
  input  [31:0] in_33,
  output [31:0] out_34
);

  Multiplexer #(.select(5), .width(32), .enable("false")) multiplexer_1 (
    .in0(in_3), .in1(in_6), .in2(in_8), .in3(in_10), .in4(in_12), .in5(in_14), .in6(in_16), .in7(in_18),
    .in8(in_21), .in9(in_23), .in10(in_2), .in11(in_5), .in12(in_7), .in13(in_9), .in14(in_11), .in15(in_13),
    .in16(in_15), .in17(in_24), .in18(in_25), .in19(in_26), .in20(in_27), .in21(in_28), .in22(in_29),
    .in23(in_17), .in24(in_20), .in25(in_22), .in26(in_30), .in27(in_31), .in28(in_32), .in29(in_33),
    .in30(in_1), .in31(in_4), .out(out_34), .sel(in_19));
endmodule

module regfile (
  input  reset,
  input  [31:0] write_data,
  input  reg_write,
  input  [4:0] write_reg,
  input  [4:0] rreg1,
  input  [4:0] rreg2,
  output [31:0] read_data1,
  output [31:0] read_data2
);

  wire [31:0] decoder_1_write_en, register_1_output, register_2_output, register_3_output, register_4_output,
       register_5_output, register_6_output, register_7_output, register_8_output, register_9_output,
       register_10_output, register_11_output, register_12_output, register_13_output, register_14_output,
       register_15_output, register_16_output, register_17_output, register_18_output, register_19_output,
       register_20_output, register_21_output, register_22_output, register_23_output, register_24_output,
       register_25_output, register_26_output, register_27_output, register_28_output, register_29_output,
       register_30_output, register_31_output, register_32_output;

  decoder decoder_1 (.Reg_write(reg_write), .Write_reg(write_reg), .write_en(decoder_1_write_en));
  register register_1 (.reg_in({32{1'b0}}), .enable(1'b1), .reset(1'b0), .\output (register_1_output));
  register register_2 (
    .reg_in(write_data), .enable(decoder_1_write_en[1]), .reset(reset), .\output (register_2_output));
  register register_3 (
    .reg_in(write_data), .enable(decoder_1_write_en[2]), .reset(reset), .\output (register_3_output));
  register register_4 (
    .reg_in(write_data), .enable(decoder_1_write_en[3]), .reset(reset), .\output (register_4_output));
  register register_5 (
    .reg_in(write_data), .enable(decoder_1_write_en[4]), .reset(reset), .\output (register_5_output));
  register register_6 (
    .reg_in(write_data), .enable(decoder_1_write_en[5]), .reset(reset), .\output (register_6_output));
  register register_7 (
    .reg_in(write_data), .enable(decoder_1_write_en[6]), .reset(reset), .\output (register_7_output));
  register register_8 (
    .reg_in(write_data), .enable(decoder_1_write_en[7]), .reset(reset), .\output (register_8_output));
  register register_9 (
    .reg_in(write_data), .enable(decoder_1_write_en[8]), .reset(reset), .\output (register_9_output));
  register register_10 (
    .reg_in(write_data), .enable(decoder_1_write_en[9]), .reset(reset), .\output (register_10_output));
  register register_11 (
    .reg_in(write_data), .enable(decoder_1_write_en[10]), .reset(reset), .\output (register_11_output));
  register register_12 (
    .reg_in(write_data), .enable(decoder_1_write_en[11]), .reset(reset), .\output (register_12_output));
  register register_13 (
    .reg_in(write_data), .enable(decoder_1_write_en[12]), .reset(reset), .\output (register_13_output));
  register register_14 (
    .reg_in(write_data), .enable(decoder_1_write_en[13]), .reset(reset), .\output (register_14_output));
  register register_15 (
    .reg_in(write_data), .enable(decoder_1_write_en[14]), .reset(reset), .\output (register_15_output));
  register register_16 (
    .reg_in(write_data), .enable(decoder_1_write_en[15]), .reset(reset), .\output (register_16_output));
  register register_17 (
    .reg_in(write_data), .enable(decoder_1_write_en[16]), .reset(reset), .\output (register_17_output));
  register register_18 (
    .reg_in(write_data), .enable(decoder_1_write_en[17]), .reset(reset), .\output (register_18_output));
  register register_19 (
    .reg_in(write_data), .enable(decoder_1_write_en[18]), .reset(reset), .\output (register_19_output));
  register register_20 (
    .reg_in(write_data), .enable(decoder_1_write_en[19]), .reset(reset), .\output (register_20_output));
  register register_21 (
    .reg_in(write_data), .enable(decoder_1_write_en[20]), .reset(reset), .\output (register_21_output));
  register register_22 (
    .reg_in(write_data), .enable(decoder_1_write_en[21]), .reset(reset), .\output (register_22_output));
  register register_23 (
    .reg_in(write_data), .enable(decoder_1_write_en[22]), .reset(reset), .\output (register_23_output));
  register register_24 (
    .reg_in(write_data), .enable(decoder_1_write_en[23]), .reset(reset), .\output (register_24_output));
  register register_25 (
    .reg_in(write_data), .enable(decoder_1_write_en[24]), .reset(reset), .\output (register_25_output));
  register register_26 (
    .reg_in(write_data), .enable(decoder_1_write_en[25]), .reset(reset), .\output (register_26_output));
  register register_27 (
    .reg_in(write_data), .enable(decoder_1_write_en[26]), .reset(reset), .\output (register_27_output));
  register register_28 (
    .reg_in(write_data), .enable(decoder_1_write_en[27]), .reset(reset), .\output (register_28_output));
  register register_29 (
    .reg_in(write_data), .enable(decoder_1_write_en[28]), .reset(reset), .\output (register_29_output));
  register register_30 (
    .reg_in(write_data), .enable(decoder_1_write_en[29]), .reset(reset), .\output (register_30_output));
  register register_31 (
    .reg_in(write_data), .enable(decoder_1_write_en[30]), .reset(reset), .\output (register_31_output));
  register register_32 (
    .reg_in(write_data), .enable(decoder_1_write_en[31]), .reset(reset), .\output (register_32_output));
  mux32_32to32 mux32_32to32_1 (
    .in_1(register_1_output), .in_2(register_2_output), .in_3(register_3_output), .in_4(register_4_output),
    .in_5(register_5_output), .in_6(register_6_output), .in_7(register_7_output), .in_8(register_8_output),
    .in_9(register_9_output), .in_10(register_10_output), .in_11(register_11_output),
    .in_12(register_12_output), .in_13(register_13_output), .in_14(register_14_output),
    .in_15(register_15_output), .in_16(register_16_output), .in_17(register_17_output),
    .in_18(register_18_output), .in_19(rreg1), .in_20(register_19_output), .in_21(register_20_output),
    .in_22(register_21_output), .in_23(register_22_output), .in_24(register_23_output),
    .in_25(register_24_output), .in_26(register_25_output), .in_27(register_26_output),
    .in_28(register_27_output), .in_29(register_28_output), .in_30(register_29_output),
    .in_31(register_30_output), .in_32(register_31_output), .in_33(register_32_output), .out_34(read_data1));
  mux32_32to32 mux32_32to32_2 (
    .in_1(register_1_output), .in_2(register_2_output), .in_3(register_3_output), .in_4(register_4_output),
    .in_5(register_5_output), .in_6(register_6_output), .in_7(register_7_output), .in_8(register_8_output),
    .in_9(register_9_output), .in_10(register_10_output), .in_11(register_11_output),
    .in_12(register_12_output), .in_13(register_13_output), .in_14(register_14_output),
    .in_15(register_15_output), .in_16(register_16_output), .in_17(register_17_output),
    .in_18(register_18_output), .in_19(rreg2), .in_20(register_19_output), .in_21(register_20_output),
    .in_22(register_21_output), .in_23(register_22_output), .in_24(register_23_output),
    .in_25(register_24_output), .in_26(register_25_output), .in_27(register_26_output),
    .in_28(register_27_output), .in_29(register_28_output), .in_30(register_29_output),
    .in_31(register_30_output), .in_32(register_31_output), .in_33(register_32_output), .out_34(read_data2));
endmodule

// instr
module instr_mem (
  input  [31:0] addr,
  output [31:0] instr
);

  wire [31:0] shifter_1_out;

  Shifter #(.width(32), .shift("lr")) shifter_1 (.in(addr), .\dist (5'b00010), .out(shifter_1_out));
  ROM #(.addrWidth(24), .dataWidth(32)) rom_1 (.addr(shifter_1_out[23:0]), .data(instr));  // open: sel

  // Notes on the sheet:
  //   contents of rom_1 (hex, n*v repeats v):
  //   38100003 38110004 8000005 38100001 38110001 2309022 1611fffc 2119820 ae530010 8e540010 214a82a
  //   8e530010 3a530001 3ab50001 2a00008
endmodule

module working (
  input  reset
);

  wire alu_1_carryout, alu_1_negative, alu_1_overflow, alu_1_zero, and_2_out, and_3_out, and_4_out,
       cu_alu_src, cu_branch, cu_jump, cu_mem_read, cu_mem_to_reg, cu_mem_write, cu_reg_write, cu_regdst,
       cu_sign_zero, discard_instr_1_id_flush, discard_instr_1_if_flush, flushblock_id_alusrc,
       flushblock_id_branch, flushblock_id_jrcontrol, flushblock_id_memread, flushblock_id_memtoreg,
       flushblock_id_memwrite, flushblock_id_regdst, flushblock_id_regwrite, jrCU_jr_control, not_1_out,
       not_2_out, not_3_out, or_1_out, reg1bit_bitout, reg_1bit_1_bitout, reg_1bit_2_bitout,
       reg_1bit_3_bitout, reg_1bit_4_bitout, reg_1bit_5_bitout, reg_1bit_6_bitout, reg_1bit_7_bitout,
       reg_1bit_8_bitout, reg_1bit_11_bitout, reg_1bit_12_bitout, reg_1bit_13_bitout, reg_1bit_14_bitout,
       reg_1bit_25_bitout, reg_1bit_26_bitout, scu_1_ifid_writeen, scu_1_pc_writeen, scu_1_stall_flush;
  wire [1:0] alu_control_unit_1_alu_control, cu_alu_op, flushblock_id_aluop_1_0, forwading_unit_1_forwarda,
       forwading_unit_1_forwardb, reg_1bit_9_bitout;
  wire [3:0] register_2_output_2;
  wire [4:0] reg_1bit_15_bitout, reg_1bit_20_bitout, select_write_regis_1_o;
  wire [27:0] register_2_output;
  wire [31:0] alu_1_output, and_1_out, bit_extender_1_out, data_memory_1_data, instr_mem_1_instr,
       mux2_32_32_1_dataout, mux2_32_32_2_dataout, mux2_32_32_3_dataout, mux2_32_32_4_dataout,
       mux3_32_32_1_out_5, mux3_32_32_2_out_5, mux_2_dataout, mux_dataout, n32bit_adder_1_out_4,
       regfile_read_data1, regfile_read_data2, register_1_output, register_3_output, register_4_output,
       register_5_output, register_6_output, register_7_output, register_8_output, register_9_output,
       register_10_output, register_11_output, register_12_output, shift_left_by2_1_out,
       shift_left_by2_2_out, sign_ext_out, undriven, wb_forward_readdata1out_31_0,
       wb_forward_readdata2out_31_0, zero_ext_out_2;

  // Probe on register_1_output
  register register_1 (
    .reg_in(mux2_32_32_4_dataout), .enable(scu_1_pc_writeen), .reset(reset), .\output (register_1_output));
  instr_mem instr_mem_1 (.addr(register_1_output), .instr(instr_mem_1_instr));
  _32bit_adder u_32bit_adder_1 (
    .in_2(register_1_output), .in_3(32'h4), .Cin(1'b0), .out_4(n32bit_adder_1_out_4));  // open: Cout
  reg_1bit reg1bit (
    .write_enable(scu_1_ifid_writeen), .bit_data(discard_instr_1_if_flush), .reset(reset),
    .bitout(reg1bit_bitout));
  register register_2 (
    .reg_in(n32bit_adder_1_out_4), .enable(scu_1_ifid_writeen), .reset(reset),
    .\output ({register_2_output_2, register_2_output}));
  register register_3 (
    .reg_in(instr_mem_1_instr), .enable(scu_1_ifid_writeen), .reset(reset), .\output (register_3_output));
  regfile regfile (
    .reset(reset), .write_data(mux2_32_32_1_dataout), .reg_write(reg_1bit_26_bitout),
    .write_reg(reg_1bit_20_bitout), .read_data1(regfile_read_data1), .read_data2(regfile_read_data2),
    .rreg1(register_3_output[25:21]), .rreg2(register_3_output[20:16]));
  sign_extender sign_ext (.In(register_3_output[15:0]), .Out(sign_ext_out));
  zero_extension zero_ext (.in_1(register_3_output[15:0]), .out_2(zero_ext_out_2));
  control_unit cu (
    .Opcode(register_3_output[31:26]), .Alu_op(cu_alu_op), .RegDst(cu_regdst), .Mem_to_reg(cu_mem_to_reg),
    .Mem_read(cu_mem_read), .Mem_Write(cu_mem_write), .jump(cu_jump), .Branch(cu_branch),
    .Sign_zero(cu_sign_zero), .Alu_Src(cu_alu_src), .Reg_write(cu_reg_write));
  mux2_32_32 mux (.Data0(sign_ext_out), .Data1(zero_ext_out_2), .select(cu_sign_zero), .Dataout(mux_dataout));
  Wb wb_forward (
    .ReadData1_31_0(regfile_read_data1), .rs_4_0(register_3_output[25:21]), .RegWrite(reg_1bit_26_bitout),
    .WriteRegister_4_0(reg_1bit_20_bitout), .ReadData2_31_0(regfile_read_data2),
    .rt_4_0(register_3_output[20:16]), .WriteData1_31_0(mux2_32_32_1_dataout),
    .ReadData1Out_31_0(wb_forward_readdata1out_31_0), .ReadData2Out_31_0(wb_forward_readdata2out_31_0));
  jr_control_unit jrCU (.Alu_op(cu_alu_op), .Func(register_3_output[5:0]), .Jr_control(jrCU_jr_control));
  discard_instr discard_instr_1 (
    .jump(cu_jump), .bne(and_2_out), .jr(reg_1bit_8_bitout), .if_flush(discard_instr_1_if_flush),
    .id_flush(discard_instr_1_id_flush));
  or or_1 (or_1_out, discard_instr_1_id_flush, reg1bit_bitout, scu_1_stall_flush);
  register register_4 (
    .reg_in({register_2_output_2, register_2_output}), .enable(1'b1), .reset(reset),
    .\output (register_4_output));
  Fcu_circuit flushblock (
    .in_1(cu_regdst), .ALUSrc(cu_alu_src), .MemtoReg(cu_mem_to_reg), .RegWrite(cu_reg_write),
    .MemRead(cu_mem_read), .MemWrite(cu_mem_write), .in_7(cu_branch), .in_8(jrCU_jr_control),
    .ALUOp_1_0(cu_alu_op), .flush(or_1_out), .ID_RegDst(flushblock_id_regdst),
    .ID_ALUSrc(flushblock_id_alusrc), .ID_MemtoReg(flushblock_id_memtoreg),
    .ID_RegWrite(flushblock_id_regwrite), .ID_MemRead(flushblock_id_memread),
    .ID_MemWrite(flushblock_id_memwrite), .ID_Branch(flushblock_id_branch),
    .ID_JRControl(flushblock_id_jrcontrol), .ID_ALUOp_1_0(flushblock_id_aluop_1_0));
  register register_5 (
    .reg_in(wb_forward_readdata1out_31_0), .enable(1'b1), .reset(reset), .\output (register_5_output));
  register register_6 (
    .reg_in(wb_forward_readdata2out_31_0), .enable(1'b1), .reset(reset), .\output (register_6_output));
  register register_7 (.reg_in(mux_dataout), .enable(1'b1), .reset(reset), .\output (register_7_output));
  register register_8 (.reg_in(register_3_output), .enable(1'b1), .reset(reset), .\output (register_8_output));
  reg_1bit reg_1bit_1 (.write_enable(1'b1), .bit_data(flushblock_id_regdst), .reset(reset), .bitout(reg_1bit_1_bitout));
  reg_1bit reg_1bit_2 (.write_enable(1'b1), .bit_data(flushblock_id_alusrc), .reset(reset), .bitout(reg_1bit_2_bitout));
  reg_1bit reg_1bit_3 (
    .write_enable(1'b1), .bit_data(flushblock_id_memtoreg), .reset(reset), .bitout(reg_1bit_3_bitout));
  reg_1bit reg_1bit_4 (
    .write_enable(1'b1), .bit_data(flushblock_id_regwrite), .reset(reset), .bitout(reg_1bit_4_bitout));
  reg_1bit reg_1bit_5 (
    .write_enable(1'b1), .bit_data(flushblock_id_memread), .reset(reset), .bitout(reg_1bit_5_bitout));
  reg_1bit reg_1bit_6 (
    .write_enable(1'b1), .bit_data(flushblock_id_memwrite), .reset(reset), .bitout(reg_1bit_6_bitout));
  reg_1bit reg_1bit_7 (.write_enable(1'b1), .bit_data(flushblock_id_branch), .reset(reset), .bitout(reg_1bit_7_bitout));
  reg_1bit reg_1bit_8 (
    .write_enable(1'b1), .bit_data(flushblock_id_jrcontrol), .reset(reset), .bitout(reg_1bit_8_bitout));
  reg_1bit reg_1bit_9 (
    .write_enable(1'b1), .bit_data(flushblock_id_aluop_1_0[0]), .reset(reset), .bitout(reg_1bit_9_bitout[0]));
  reg_1bit reg_1bit_10 (
    .write_enable(1'b1), .bit_data(flushblock_id_aluop_1_0[1]), .reset(reset), .bitout(reg_1bit_9_bitout[1]));
  Forwading_unit forwading_unit_1 (
    .EX_rt_4_0(register_8_output[20:16]), .Ex_rs_4_0(register_8_output[25:21]),
    .MEM_WriteRegister_4_0(reg_1bit_15_bitout), .WB_WriteRegister_4_0(reg_1bit_20_bitout),
    .WB_RegWrite(reg_1bit_26_bitout), .MEM_RegWrite(reg_1bit_12_bitout),
    .ForwardA(forwading_unit_1_forwarda), .ForwardB(forwading_unit_1_forwardb));
  mux3_32_32 mux3_32_32_1 (
    .A__31_0(register_5_output), .B__31_0(undriven), .C__31_0(register_3_output),
    .Select__1_0(forwading_unit_1_forwarda), .out_5(mux3_32_32_1_out_5));
  mux2_32_32 mux_2 (
    .Data0(mux3_32_32_2_out_5), .Data1(register_7_output), .select(reg_1bit_2_bitout), .Dataout(mux_2_dataout));
  mux3_32_32 mux3_32_32_2 (
    .A__31_0(register_6_output), .B__31_0(undriven), .C__31_0(register_3_output),
    .Select__1_0(forwading_unit_1_forwardb), .out_5(mux3_32_32_2_out_5));
  alu_control_unit alu_control_unit_1 (
    .Alu_op(reg_1bit_9_bitout), .Func(register_7_output[5:0]), .Alu_control(alu_control_unit_1_alu_control));
  alu alu_1 (
    .BUSSA(mux3_32_32_1_out_5), .BUSSB(mux_2_dataout), .ALUControl(alu_control_unit_1_alu_control),
    .Output(alu_1_output), .negative(alu_1_negative), .overflow(alu_1_overflow), .carryout(alu_1_carryout),
    .Zero(alu_1_zero));
  select_write_regis select_write_regis_1 (
    .A(register_8_output[20:16]), .B(register_8_output[15:11]), .select(reg_1bit_1_bitout),
    .O(select_write_regis_1_o));
  register register_9 (.reg_in(alu_1_output), .enable(1'b1), .reset(reset), .\output (register_9_output));
  register register_10 (.reg_in(mux3_32_32_2_out_5), .enable(1'b1), .reset(reset), .\output (register_10_output));
  reg_1bit reg_1bit_11 (.write_enable(reg_1bit_3_bitout), .bit_data(1'b1), .reset(reset), .bitout(reg_1bit_11_bitout));
  reg_1bit reg_1bit_12 (.write_enable(reg_1bit_4_bitout), .bit_data(1'b1), .reset(reset), .bitout(reg_1bit_12_bitout));
  reg_1bit reg_1bit_13 (.write_enable(reg_1bit_5_bitout), .bit_data(1'b1), .reset(reset), .bitout(reg_1bit_13_bitout));
  reg_1bit reg_1bit_14 (.write_enable(reg_1bit_6_bitout), .bit_data(1'b1), .reset(reset), .bitout(reg_1bit_14_bitout));
  reg_1bit reg_1bit_15 (
    .write_enable(select_write_regis_1_o[0]), .bit_data(1'b1), .reset(reset), .bitout(reg_1bit_15_bitout[0]));
  reg_1bit reg_1bit_16 (
    .write_enable(select_write_regis_1_o[1]), .bit_data(1'b1), .reset(reset), .bitout(reg_1bit_15_bitout[1]));
  reg_1bit reg_1bit_17 (
    .write_enable(select_write_regis_1_o[2]), .bit_data(1'b1), .reset(reset), .bitout(reg_1bit_15_bitout[2]));
  reg_1bit reg_1bit_18 (
    .write_enable(select_write_regis_1_o[3]), .bit_data(1'b1), .reset(reset), .bitout(reg_1bit_15_bitout[3]));
  reg_1bit reg_1bit_19 (
    .write_enable(select_write_regis_1_o[4]), .bit_data(1'b1), .reset(reset), .bitout(reg_1bit_15_bitout[4]));
  data_memory data_memory_1 (
    .addr(register_9_output), .write_data(register_10_output), .write_enable(reg_1bit_14_bitout),
    .data(data_memory_1_data));
  register register_11 (.reg_in(data_memory_1_data), .enable(1'b1), .reset(reset), .\output (register_11_output));
  register register_12 (.reg_in(register_9_output), .enable(1'b1), .reset(reset), .\output (register_12_output));
  reg_1bit reg_1bit_20 (
    .write_enable(reg_1bit_15_bitout[0]), .bit_data(1'b1), .reset(reset), .bitout(reg_1bit_20_bitout[0]));
  reg_1bit reg_1bit_21 (
    .write_enable(reg_1bit_15_bitout[1]), .bit_data(1'b1), .reset(reset), .bitout(reg_1bit_20_bitout[1]));
  reg_1bit reg_1bit_22 (
    .write_enable(reg_1bit_15_bitout[2]), .bit_data(1'b1), .reset(reset), .bitout(reg_1bit_20_bitout[2]));
  reg_1bit reg_1bit_23 (
    .write_enable(reg_1bit_15_bitout[3]), .bit_data(1'b1), .reset(reset), .bitout(reg_1bit_20_bitout[3]));
  reg_1bit reg_1bit_24 (
    .write_enable(reg_1bit_15_bitout[4]), .bit_data(1'b1), .reset(reset), .bitout(reg_1bit_20_bitout[4]));
  reg_1bit reg_1bit_25 (.write_enable(reg_1bit_11_bitout), .bit_data(1'b1), .reset(reset), .bitout(reg_1bit_25_bitout));
  reg_1bit reg_1bit_26 (.write_enable(reg_1bit_12_bitout), .bit_data(1'b1), .reset(reset), .bitout(reg_1bit_26_bitout));
  mux2_32_32 mux2_32_32_1 (
    .Data0(register_12_output), .Data1(register_11_output), .select(reg_1bit_25_bitout),
    .Dataout(mux2_32_32_1_dataout));
  scu scu_1 (
    .in_1(register_3_output[31:26]), .EX_MemRead(reg_1bit_5_bitout), .in_3(register_3_output[25:21]),
    .in_4(register_8_output[20:16]), .in_5(register_3_output[20:16]), .Stall_flush(scu_1_stall_flush),
    .IFID_WriteEn(scu_1_ifid_writeen), .PC_WriteEn(scu_1_pc_writeen));
  shift_left_by2 shift_left_by2_1 (.In(mux_dataout), .Out(shift_left_by2_1_out));
  not not_1 (not_1_out, alu_1_zero);
  assign bit_extender_1_out = {{6{1'b0}}, register_3_output[25:0]};  // Bit_Extender bit_extender_1
  assign and_1_out = shift_left_by2_1_out & register_4_output;  // AND_Gate and_1, 32 bits wide
  and and_2 (and_2_out, not_1_out, reg_1bit_7_bitout);
  mux2_32_32 mux2_32_32_2 (
    .Data0(n32bit_adder_1_out_4), .Data1(and_1_out), .select(and_2_out), .Dataout(mux2_32_32_2_dataout));
  shift_left_by2 shift_left_by2_2 (.In(bit_extender_1_out), .Out(shift_left_by2_2_out));
  not not_2 (not_2_out, reg1bit_bitout);
  not not_3 (not_3_out, and_2_out);
  and and_3 (and_3_out, not_2_out, cu_jump);
  and and_4 (and_4_out, not_3_out, and_3_out);
  mux2_32_32 mux2_32_32_3 (
    .Data0(mux2_32_32_2_dataout), .Data1({shift_left_by2_2_out[27:0], register_2_output_2}),
    .select(and_4_out), .Dataout(mux2_32_32_3_dataout));
  mux2_32_32 mux2_32_32_4 (
    .Data0(mux2_32_32_3_dataout), .Data1(mux3_32_32_1_out_5), .select(reg_1bit_8_bitout),
    .Dataout(mux2_32_32_4_dataout));

  // Notes on the sheet:
  //   pcin
  //   ifid_writeen
  //   if_flush
  //   ifid_flush
  //   idpc4
  //   id_instr
  //   wb_reg_write
  //   wb_write_data
  //   imm16
  //   rt
  //   rs
  //   func
  //   wb_write_reg
  //   opcode
  //   imm16ext
  //   aluop
  //   signzero
  //   jrCOntrol
  //   read_data1out
  //   read_data2
  //   if_flush
  //   id_flush
  //   ifid flush
  //   stall_flush
  //   reset
  //   flush
  //   ex_pc4
  //   ex_readdata1
  //   exread_data2
  //   ex_imm16ext
  //   ex_instr
  //   ex_reg_dest
  //   ex_alusrc
  //   ex_memtoreg
  //   ex_regwrite
  //   ex_memread
  //   ex_memwrite
  //   ex_branch
  //   ex_jrcontrol
  //   ex_aluop0
  //   ex_aluop1
  //   mem_writereg
  //   mem_regwrite
  //   ex_rd
  //   ex_rt
  //   ex_rs
  //   forwarding_unit
  //   mem_alu_result
  //   forwardA
  //   forwardB
  //   mux
  //   mux
  //   busA_alu
  //   busB_forwarded
  //   busB_alu
  //   alu_control
  //   ex_alures
  //   negative_flag
  //   overflow_flag
  //   carryout
  //   zero_flag
  //   mux
  //   ex_writereg
  //   register
  //   reg1bit
  //   mem_alures
  //   writedataofmem
  //   mem_memtoreg
  //   mem_regwrite
  //   mem_memread
  //   mem_memwrite
  //   mem_writereg0
  //   mem_writereg1
  //   mem_writereg2
  //   mem_writereg3
  //   mem_writereg4
  //   mem_readdataofmem
  //   register
  //   reg1bit
  //   mem_writereg
  //   wb_readdataofmem
  //   wb_aluresult
  //   wb_writereg0
  //   wb_writereg1
  //   wb_writereg2
  //   wb_writereg3
  //   wb_writereg4
  //   wb_memtoreg
  //   wb_regwrite
  //   wb_writereg
  //   wb_writedata
  //   pc_writeen
  //   stall_flush
  //   if_id_writeen
  //   shiftleftby2bneout
  //   not_zeroflag
  //   pcbne
  //   bne_control
  //   pc4bne
  //   shiftleft2_jump_out
  //   pcj
  //   not_ifidflush
  //   jump_flush
  //   pcjr
  //   jump_control
  //   pc4bnej
  //   pcin
endmodule

module discard_instr (
  input  jump,
  input  bne,
  input  jr,
  output if_flush,
  output id_flush
);

  or or_1 (if_flush, jump, bne, jr);
  or or_2 (id_flush, bne, jr);
endmodule
